// Logisim project cpu.circ as structural Verilog: 3 circuits, main circuit main
module main (
  input  [31:0] INSTRUCTION,
  input  CLOCK,
  output [31:0] FETCH_ADDRESS,
  output [31:0] s0_Value,
  output [31:0] s1_Value,
  output [31:0] s2_Value,
  output [31:0] ra_Value,
  output [31:0] HI_Value,
  output [31:0] LO_Value
);

  wire ALUSrc, and_1_out, and_2_out, Branch, equal, Jump, JumpReg, main_2_signed_overflow, MemWrite,
       multiplexer_3_out, not_1_out, RegWrite, Shift;
  wire [1:0] ALUOp, MemtoReg, Move, RegDst;
  wire [2:0] Unit;
  wire [3:0] ALUctr;
  wire [4:0] multiplexer_1_out;
  wire [5:0] funct, opcode;
  wire [25:6] Inst_25_0;
  wire [27:0] bit_extender_1_out, JumpAddr;
  wire [31:0] _32_bit_Im, _32_bit_Shamt, adder_3_out, FinalAddr, Lo_Hi, lui, main_1_read_data_1, MEM_p6,
       multiplexer_4_out, multiplexer_5_out, multiplexer_6_out, multiplexer_7_out, multiplexer_9_out, PC_4,
       R2, result, result_2, shifter_1_out, swinc, WriteData, X;

  // Probe on RegDst
  Register #(.width(32)) PC (.D(FinalAddr), .Q(FETCH_ADDRESS), .clk(CLOCK));  // open: en, clr
  Multiplexer #(.select(2), .width(5)) multiplexer_1 (
    .in0(Inst_25_0[20:16]), .in1(Inst_25_0[15:11]), .in2({5{1'b1}}), .in3(Inst_25_0[25:21]),
    .out(multiplexer_1_out), .sel(RegDst));  // open: en
  Adder #(.width(32)) adder_1 (.a(FETCH_ADDRESS), .b(32'h4), .out(PC_4));  // open: cin, cout
  Register #(.width(32)) HI (.Q(HI_Value), .clk(CLOCK));  // open: D, en, clr
  regfile_main main_1 (
    .Read_Register_1(Inst_25_0[25:21]), .Read_Register_2(Inst_25_0[20:16]),
    .Write_Register(multiplexer_1_out), .Write_Data(WriteData), .Write_Enable(RegWrite), .Clock(CLOCK),
    .Read_Data_1(main_1_read_data_1), .Read_Data_2(R2), .s0_Value(s0_Value), .s1_Value(s1_Value),
    .s2_Value(s2_Value), .ra_Value(ra_Value));
  Register #(.width(32)) register_1 (.D(INSTRUCTION), .Q({opcode, Inst_25_0, funct}), .clk(CLOCK));  // open: en, clr
  Adder #(.width(32)) adder_2 (.a(_32_bit_Im), .b(main_1_read_data_1), .out(swinc));  // open: cin, cout
  Register #(.width(32)) LO (.Q(LO_Value), .clk(CLOCK));  // open: D, en, clr
  Shifter #(.width(32)) shifter_1 (.in(_32_bit_Im), .\dist (5'b00010), .out(shifter_1_out));
  Multiplexer #(.width(32)) multiplexer_2 (.in0(main_1_read_data_1), .in1(R2), .out(X), .sel(Shift));  // open: en
  and and_1 (and_1_out, equal, Branch);
  not not_1 (not_1_out, equal);
  and and_2 (and_2_out, not_1_out, Branch);
  Adder #(.width(32)) adder_3 (.a(FETCH_ADDRESS), .b(shifter_1_out), .out(adder_3_out));  // open: cin, cout
  Multiplexer multiplexer_3 (.in0(and_1_out), .in1(and_2_out), .out(multiplexer_3_out), .sel(ALUOp[1]));  // open: en
  Multiplexer #(.width(32)) multiplexer_4 (
    .in0(R2), .in1(_32_bit_Shamt), .out(multiplexer_4_out), .sel(Shift));  // open: en
  MainControlUnit maincontrolunit_1 (
    .Opcode(opcode), .RegDst(RegDst), .Jump(Jump), .Branch(Branch), .MemtoReg(MemtoReg), .ALUOp(ALUOp),
    .MemWrite(MemWrite), .ALUSrc(ALUSrc), .RegWrite(RegWrite), .Unit(Unit));
  ALUcontrol alucontrol_1 (
    .ALUOp(ALUOp), .opcode(opcode), .funct(funct), .ALUctr(ALUctr), .JumpReg(JumpReg), .Move(Move),
    .Shift(Shift));
  Multiplexer #(.width(32)) multiplexer_5 (
    .in0(PC_4), .in1(adder_3_out), .out(multiplexer_5_out), .sel(multiplexer_3_out));  // open: en
  Multiplexer #(.width(32)) multiplexer_6 (
    .in0(multiplexer_4_out), .in1(_32_bit_Im), .out(multiplexer_6_out), .sel(ALUSrc));  // open: en
  assign bit_extender_1_out = {{2{1'b0}}, {Inst_25_0, funct}};  // Bit_Extender bit_extender_1
  LED led_1 (.in(main_2_signed_overflow));
  alu_main main_2 (
    .Switch(ALUctr), .X(X), .Equal(equal), .Result(result), .Signed_Overflow(main_2_signed_overflow),
    .Y(multiplexer_6_out), .Result_2(result_2));
  // Probe on ALUctr
  Shifter #(.width(28)) shifter_2 (.in(bit_extender_1_out), .\dist (5'b00010), .out(JumpAddr));
  Multiplexer #(.width(32)) multiplexer_7 (
    .in0(multiplexer_5_out), .in1({FETCH_ADDRESS[31:28], JumpAddr}), .out(multiplexer_7_out), .sel(Jump));  // open: en
  Shifter #(.width(32)) shifter_3 (.in(_32_bit_Im), .\dist (5'b10000), .out(lui));
  assign _32_bit_Im = {{16{Inst_25_0[15]}}, {Inst_25_0[15:6], funct}};  // Bit_Extender bit_extender_2
  assign _32_bit_Shamt = {{27{1'b0}}, Inst_25_0[10:6]};  // Bit_Extender bit_extender_3
  // Probe on {FETCH_ADDRESS[31:28], JumpAddr}
  // Probe on FinalAddr
  Multiplexer #(.width(32)) multiplexer_8 (
    .in0(multiplexer_7_out), .in1(X), .out(FinalAddr), .sel(JumpReg));  // open: en
  // mem_main MEM: pin names not known; wires that end beside it: result, R2, MemWrite, CLOCK, Unit, MEM_p6
  // Probe on Unit
  Multiplexer #(.width(32)) multiplexer_9 (
    .in0(result), .in1(Lo_Hi), .out(multiplexer_9_out), .sel(Move[0]));  // open: en
  Multiplexer #(.width(32)) multiplexer_10 (.in0(LO_Value), .in1(HI_Value), .out(Lo_Hi), .sel(Move[0]));  // open: en
  Multiplexer #(.select(2), .width(32)) multiplexer_11 (
    .in0(multiplexer_9_out), .in1(MEM_p6), .in2(PC_4), .in3(lui), .out(WriteData), .sel(MemtoReg));  // open: en
  // Probe on MemtoReg

  // Other names for the same wires on the sheet: Inst_25_0[5:0] = funct; shamt[4:0] = Inst_25_0[10:6];
  //   rd[4:0] = Inst_25_0[15:11]; clk = CLOCK; fetch_addr[31:0] = FETCH_ADDRESS; HI[31:0] = HI_Value;
  //   rt[4:0] = Inst_25_0[20:16]; rs[4:0] = Inst_25_0[25:21]; JumpAddr[31:28] = FETCH_ADDRESS[31:28];
  //   LO[31:0] = LO_Value; ra[31:0] = ra_Value; s0[31:0] = s0_Value; s1[31:0] = s1_Value; s2[31:0] = s2_Value

  // Notes on the sheet:
  //   Output
  //   These are outputs/inputs from run.circ
  //   Inputs
  //   These are DEBUG/TEST outputs from your circuit.
endmodule

module ALUcontrol (
  input  [1:0] ALUOp,
  input  [5:0] opcode,
  input  [5:0] funct,
  output [3:0] ALUctr,
  output JumpReg,
  output [1:0] Move,
  output Shift
);

  wire ALUOp_00, ALUOp_10, and_12_out, and_13_out, and_14_out, and_15_out, and_29_out, and_30_out,
       and_31_out, and_32_out, f0, f1, f2, f3, f4, f5, func2, func3, func4, func5, func6, func7, func11,
       func17, func18, func19, func20, func21, func22, func24, func25, func26, func27, func28, func29,
       func30, func31, func32, func33, func34, func35, not_1_out, not_2_out, not_3_out, not_4_out, not_5_out,
       not_6_out, not_7_out, not_8_out, not_9_out, not_10_out, not_11_out, not_12_out, not_13_out,
       not_14_out, not_15_out, not_16_out, not_17_out, not_18_out, not_19_out, not_20_out, not_21_out,
       not_22_out, not_23_out, not_24_out, not_25_out, not_26_out, not_27_out, not_28_out, not_29_out,
       not_30_out, not_31_out, not_32_out, not_33_out, not_34_out, not_35_out, not_36_out, not_37_out,
       not_38_out, not_39_out, not_40_out, not_41_out, not_42_out, not_43_out, not_44_out, not_45_out,
       not_46_out, not_47_out, not_48_out, not_49_out, not_50_out, not_51_out, not_52_out, not_53_out,
       not_54_out, not_55_out, not_56_out, not_57_out, not_58_out, not_59_out, not_60_out, not_61_out,
       not_62_out, not_63_out, not_64_out, not_65_out, not_66_out, not_67_out, not_68_out, not_69_out,
       not_70_out, not_71_out, not_72_out, not_73_out, not_74_out, not_75_out, not_76_out, not_77_out,
       not_78_out, not_79_out, not_80_out, not_81_out, not_82_out, not_83_out, not_84_out, not_85_out,
       not_86_out, not_87_out, not_88_out, not_89_out, not_90_out, not_91_out, not_92_out, not_93_out,
       not_94_out, or_1_out, or_2_out, or_3_out, or_4_out, or_5_out, or_6_out, or_9_out, or_10_out,
       or_11_out, or_12_out;

  not not_1 (not_1_out, f0);
  not not_2 (not_2_out, f1);
  not not_3 (not_3_out, f2);
  not not_4 (not_4_out, f3);
  not not_5 (not_5_out, f4);
  not not_6 (not_6_out, f1);
  not not_7 (not_7_out, f2);
  not not_8 (not_8_out, f3);
  not not_9 (not_9_out, f4);
  not not_10 (not_10_out, f2);
  not not_11 (not_11_out, f5);
  not not_12 (not_12_out, f2);
  not not_13 (not_13_out, f3);
  not not_14 (not_14_out, f4);
  not not_15 (not_15_out, f0);
  not not_16 (not_16_out, f1);
  not not_17 (not_17_out, f2);
  not not_18 (not_18_out, f3);
  not not_19 (not_19_out, f5);
  not not_20 (not_20_out, f0);
  not not_21 (not_21_out, f2);
  not not_22 (not_22_out, f4);
  not not_23 (not_23_out, f0);
  not not_24 (not_24_out, f1);
  not not_25 (not_25_out, f2);
  not not_26 (not_26_out, f3);
  not not_27 (not_27_out, f4);
  not not_28 (not_28_out, f5);
  not not_29 (not_29_out, f0);
  not not_30 (not_30_out, f1);
  not not_31 (not_31_out, f2);
  not not_32 (not_32_out, f4);
  not not_33 (not_33_out, f0);
  not not_34 (not_34_out, f1);
  not not_35 (not_35_out, f4);
  not not_36 (not_36_out, ALUOp[0]);
  not not_37 (not_37_out, ALUOp[0]);
  not not_38 (not_38_out, ALUOp[1]);
  and and_1 (func2, not_1_out, not_2_out, not_3_out, not_4_out, not_5_out, f5);
  and and_2 (func5, f0, not_6_out, not_7_out, not_8_out, not_9_out, f5);
  and and_3 (func11, f0, f1, not_10_out, f3, f4, not_11_out);
  and and_4 (func19, f0, f1, not_12_out, not_13_out, not_14_out, f5);
  and and_5 (func21, not_15_out, not_16_out, not_17_out, not_18_out, f4, not_19_out);
  and and_6 (func25, not_20_out, f1, not_21_out, f3, not_22_out, f5);
  and and_7 (func28, not_23_out, not_24_out, not_25_out, not_26_out, not_27_out, not_28_out);
  and and_8 (func31, not_29_out, not_30_out, not_31_out, f3, not_32_out, f5);
  and and_9 (func34, not_33_out, not_34_out, f2, f3, not_35_out, f5);
  and and_10 (ALUOp_10, not_36_out, ALUOp[1]);
  and and_11 (ALUOp_00, not_37_out, not_38_out);
  or or_1 (or_1_out, func3, func7, func26);
  and and_12 (and_12_out, ALUOp_10, or_2_out);
  or or_2 (or_2_out, func2, func6, func20, func25, func30, func35);
  and and_13 (and_13_out, ALUOp_00, or_1_out);
  and and_14 (and_14_out, ALUOp_10, or_3_out);
  or or_3 (or_3_out, func2, func5, func11, func27, func35);
  and and_15 (and_15_out, ALUOp_00, or_4_out);
  or or_4 (or_4_out, func4, func2, func6, func17, func18, func19, func3, func31, func32, func33, func34);
  or or_5 (or_5_out, func21, func22);
  or or_6 (or_6_out, func28, func29, func30);
  or or_7 (ALUctr[0], and_12_out, and_13_out);
  or or_8 (ALUctr[2], and_14_out, and_15_out);
  and and_16 (JumpReg, ALUOp_10, func3);
  and and_17 (Move[0], ALUOp_10, func21);
  and and_18 (Move[1], ALUOp_10, or_5_out);
  and and_19 (Shift, ALUOp_10, or_6_out);
  not not_39 (not_39_out, f0);
  not not_40 (not_40_out, f1);
  not not_41 (not_41_out, f2);
  not not_42 (not_42_out, f4);
  not not_43 (not_43_out, f5);
  not not_44 (not_44_out, f0);
  not not_45 (not_45_out, f1);
  not not_46 (not_46_out, f3);
  not not_47 (not_47_out, f4);
  not not_48 (not_48_out, f1);
  not not_49 (not_49_out, f3);
  not not_50 (not_50_out, f4);
  not not_51 (not_51_out, f1);
  not not_52 (not_52_out, f2);
  not not_53 (not_53_out, f5);
  not not_54 (not_54_out, f0);
  not not_55 (not_55_out, f2);
  not not_56 (not_56_out, f3);
  not not_57 (not_57_out, f5);
  not not_58 (not_58_out, f0);
  not not_59 (not_59_out, f2);
  not not_60 (not_60_out, f4);
  not not_61 (not_61_out, f5);
  not not_62 (not_62_out, f2);
  not not_63 (not_63_out, f3);
  not not_64 (not_64_out, f4);
  not not_65 (not_65_out, f5);
  not not_66 (not_66_out, f1);
  not not_67 (not_67_out, f2);
  not not_68 (not_68_out, f4);
  not not_69 (not_69_out, f0);
  not not_70 (not_70_out, f2);
  not not_71 (not_71_out, f3);
  not not_72 (not_72_out, f4);
  Multiplexer #(.width(6)) multiplexer_1 (
    .in0(opcode), .in1(funct), .out({f5, f4, f3, f2, f1, f0}), .sel(ALUOp[1]));  // open: en
  and and_20 (func3, not_39_out, not_40_out, not_41_out, f3, not_42_out, not_43_out);
  and and_21 (func6, not_44_out, not_45_out, f2, not_46_out, not_47_out, f5);
  and and_22 (func17, f0, not_48_out, f2, not_49_out, not_50_out, f5);
  and and_23 (func20, f0, not_51_out, not_52_out, f3, f4, not_53_out);
  and and_24 (func22, not_54_out, f1, not_55_out, not_56_out, f4, not_57_out);
  and and_25 (func26, not_58_out, f1, not_59_out, f3, not_60_out, not_61_out);
  and and_26 (func29, f0, f1, not_62_out, not_63_out, not_64_out, not_65_out);
  and and_27 (func32, f0, not_66_out, not_67_out, f3, not_68_out, f5);
  and and_28 (func35, not_69_out, f1, not_70_out, not_71_out, not_72_out, f5);
  or or_9 (or_9_out, func5, func20, func17, func25, func29, func35);
  or or_10 (or_10_out, func4, func2, func6, func17, func18, func19, func24, func26, func31, func32, func33, func34);
  or or_11 (or_11_out, func6, func17, func25, func27, func19);
  or or_12 (or_12_out, func7, func24, func26);
  not not_73 (not_73_out, f1);
  not not_74 (not_74_out, f2);
  not not_75 (not_75_out, f4);
  not not_76 (not_76_out, f5);
  not not_77 (not_77_out, f0);
  not not_78 (not_78_out, f1);
  not not_79 (not_79_out, f4);
  not not_80 (not_80_out, f5);
  not not_81 (not_81_out, f4);
  not not_82 (not_82_out, f5);
  not not_83 (not_83_out, f1);
  not not_84 (not_84_out, f4);
  not not_85 (not_85_out, f5);
  not not_86 (not_86_out, f2);
  not not_87 (not_87_out, f4);
  not not_88 (not_88_out, f0);
  not not_89 (not_89_out, f2);
  not not_90 (not_90_out, f3);
  not not_91 (not_91_out, f4);
  not not_92 (not_92_out, f5);
  not not_93 (not_93_out, f2);
  not not_94 (not_94_out, f4);
  and and_29 (and_29_out, ALUOp_10, or_9_out);
  and and_30 (and_30_out, ALUOp_00, or_10_out);
  and and_31 (and_31_out, ALUOp_10, or_11_out);
  and and_32 (and_32_out, ALUOp_00, or_12_out);
  and and_33 (func4, f0, not_73_out, not_74_out, f3, not_75_out, not_76_out);
  and and_34 (func7, not_77_out, not_78_out, f2, f3, not_79_out, not_80_out);
  and and_35 (func18, f0, f1, f2, f3, not_81_out, not_82_out);
  and and_36 (func24, f0, not_83_out, f2, f3, not_84_out, not_85_out);
  and and_37 (func27, f0, f1, not_86_out, f3, not_87_out, f5);
  and and_38 (func30, not_88_out, f1, not_89_out, not_90_out, not_91_out, not_92_out);
  and and_39 (func33, f0, f1, not_93_out, f3, not_94_out, f5);
  or or_13 (ALUctr[1], and_29_out, and_30_out);
  or or_14 (ALUctr[3], and_31_out, and_32_out);

  // Other names for the same wires on the sheet: func15 = func2; func14 = func3; func16 = func6; func23 = func17;
  //   func36 = func19
endmodule

module MainControlUnit (
  input  [5:0] Opcode,
  output [1:0] RegDst,
  output Jump,
  output Branch,
  output [1:0] MemtoReg,
  output [1:0] ALUOp,
  output MemWrite,
  output ALUSrc,
  output RegWrite,
  output [2:0] Unit
);

  wire and_8_out, and_12_out, and_15_out, and_16_out, FeDCba, FeDcBA_t, FeDcbA_t_t, FedCbA_t_t_t,
       FedcBA_t_t_t_t, fEdCba_t_t_t_t_t, feDCBA_t_t_t_t_t_t, fedCbA_t_t_t_t_t_t_t, fedcBA_t_t_t_t_t_t_t_t,
       fedcba_t_t_t_t_t_t_t_t_t, fXdCba, not_1_out, not_2_out, not_3_out, not_4_out, not_5_out, not_6_out,
       not_7_out, not_8_out, not_9_out, not_10_out, not_11_out, not_12_out, not_13_out, not_14_out,
       not_15_out, not_16_out, not_17_out, not_18_out, not_19_out, not_20_out, not_21_out, not_22_out,
       not_23_out, not_24_out, not_25_out, not_26_out, not_27_out, not_28_out, not_29_out, not_30_out,
       not_31_out, not_32_out, not_33_out, not_34_out, not_35_out, not_36_out, not_37_out, not_38_out,
       not_39_out, not_40_out, not_41_out, not_42_out, not_43_out, not_44_out, not_45_out, not_46_out,
       not_47_out, not_48_out, not_49_out, not_50_out, not_51_out, not_52_out, not_53_out, not_54_out,
       not_55_out, not_56_out, not_57_out, not_58_out, not_59_out, not_60_out, not_61_out, not_62_out,
       not_63_out, not_64_out, not_65_out, not_66_out, not_67_out, not_68_out, not_69_out, not_70_out,
       not_71_out, not_72_out, not_73_out, not_74_out, not_75_out, not_76_out, not_77_out, not_78_out,
       not_79_out, or_3_out, or_4_out, or_5_out, or_6_out, or_7_out, or_8_out, or_9_out, or_10_out,
       or_11_out, or_12_out;

  not not_1 (not_1_out, Opcode[0]);
  not not_2 (not_2_out, Opcode[1]);
  not not_3 (not_3_out, Opcode[2]);
  not not_4 (not_4_out, Opcode[3]);
  not not_5 (not_5_out, Opcode[4]);
  not not_6 (not_6_out, Opcode[5]);
  not not_7 (not_7_out, Opcode[0]);
  not not_8 (not_8_out, Opcode[1]);
  not not_9 (not_9_out, Opcode[4]);
  not not_10 (not_10_out, Opcode[0]);
  not not_11 (not_11_out, Opcode[1]);
  not not_12 (not_12_out, Opcode[3]);
  not not_13 (not_13_out, Opcode[5]);
  not not_14 (not_14_out, Opcode[2]);
  not not_15 (not_15_out, Opcode[3]);
  not not_16 (not_16_out, Opcode[4]);
  not not_17 (not_17_out, Opcode[5]);
  not not_18 (not_18_out, Opcode[2]);
  not not_19 (not_19_out, Opcode[3]);
  not not_20 (not_20_out, Opcode[4]);
  not not_21 (not_21_out, Opcode[5]);
  not not_22 (not_22_out, Opcode[0]);
  not not_23 (not_23_out, Opcode[1]);
  not not_24 (not_24_out, Opcode[3]);
  not not_25 (not_25_out, Opcode[5]);
  not not_26 (not_26_out, Opcode[1]);
  not not_27 (not_27_out, Opcode[3]);
  not not_28 (not_28_out, Opcode[4]);
  not not_29 (not_29_out, Opcode[5]);
  not not_30 (not_30_out, Opcode[0]);
  not not_31 (not_31_out, Opcode[1]);
  not not_32 (not_32_out, Opcode[3]);
  not not_33 (not_33_out, Opcode[4]);
  not not_34 (not_34_out, Opcode[1]);
  not not_35 (not_35_out, Opcode[3]);
  not not_36 (not_36_out, Opcode[4]);
  not not_37 (not_37_out, Opcode[4]);
  not not_38 (not_38_out, Opcode[5]);
  not not_39 (not_39_out, Opcode[2]);
  not not_40 (not_40_out, Opcode[3]);
  not not_41 (not_41_out, Opcode[4]);
  not not_42 (not_42_out, Opcode[1]);
  not not_43 (not_43_out, Opcode[2]);
  not not_44 (not_44_out, Opcode[4]);
  not not_45 (not_45_out, Opcode[2]);
  not not_46 (not_46_out, Opcode[4]);
  not not_47 (not_47_out, Opcode[0]);
  not not_48 (not_48_out, Opcode[1]);
  not not_49 (not_49_out, Opcode[4]);
  not not_50 (not_50_out, Opcode[2]);
  not not_51 (not_51_out, Opcode[2]);
  not not_52 (not_52_out, Opcode[4]);
  not not_53 (not_53_out, Opcode[0]);
  not not_54 (not_54_out, Opcode[2]);
  not not_55 (not_55_out, Opcode[2]);
  not not_56 (not_56_out, Opcode[0]);
  not not_57 (not_57_out, Opcode[2]);
  not not_58 (not_58_out, Opcode[1]);
  not not_59 (not_59_out, Opcode[3]);
  not not_60 (not_60_out, Opcode[5]);
  not not_61 (not_61_out, Opcode[0]);
  not not_62 (not_62_out, Opcode[3]);
  not not_63 (not_63_out, Opcode[5]);
  not not_64 (not_64_out, Opcode[0]);
  not not_65 (not_65_out, Opcode[1]);
  not not_66 (not_66_out, Opcode[3]);
  not not_67 (not_67_out, Opcode[5]);
  not not_68 (not_68_out, Opcode[0]);
  not not_69 (not_69_out, Opcode[1]);
  not not_70 (not_70_out, Opcode[2]);
  not not_71 (not_71_out, Opcode[3]);
  not not_72 (not_72_out, Opcode[4]);
  not not_73 (not_73_out, Opcode[0]);
  not not_74 (not_74_out, Opcode[1]);
  not not_75 (not_75_out, Opcode[2]);
  not not_76 (not_76_out, Opcode[4]);
  not not_77 (not_77_out, Opcode[1]);
  not not_78 (not_78_out, Opcode[2]);
  not not_79 (not_79_out, Opcode[4]);
  and and_1 (fedcba_t_t_t_t_t_t_t_t_t, not_1_out, not_2_out, not_3_out, not_4_out, not_5_out, not_6_out);
  and and_2 (FeDCba, not_7_out, not_8_out, Opcode[2], Opcode[3], not_9_out, Opcode[5]);
  and and_3 (fEdCba_t_t_t_t_t, not_10_out, not_11_out, Opcode[2], not_12_out, Opcode[4], not_13_out);
  and and_4 (fedcBA_t_t_t_t_t_t_t_t, Opcode[0], Opcode[1], not_14_out, not_15_out, not_16_out, not_17_out);
  and and_5 (Jump, Opcode[1], not_18_out, not_19_out, not_20_out, not_21_out);
  and and_6 (fXdCba, not_22_out, not_23_out, Opcode[2], not_24_out, not_25_out);
  and and_7 (fedCbA_t_t_t_t_t_t_t, Opcode[0], not_26_out, Opcode[2], not_27_out, not_28_out, not_29_out);
  and and_8 (and_8_out, not_30_out, not_31_out, not_32_out, not_33_out, Opcode[5]);
  and and_9 (FedCbA_t_t_t, Opcode[0], not_34_out, Opcode[2], not_35_out, not_36_out, Opcode[5]);
  and and_10 (feDCBA_t_t_t_t_t_t, Opcode[0], Opcode[1], Opcode[2], Opcode[3], not_37_out, not_38_out);
  and and_11 (FedcBA_t_t_t_t, Opcode[0], Opcode[1], not_39_out, not_40_out, not_41_out, Opcode[5]);
  or or_1 (MemtoReg[1], fEdCba_t_t_t_t_t, fedcBA_t_t_t_t_t_t_t_t, feDCBA_t_t_t_t_t_t);
  and and_12 (and_12_out, not_42_out, not_43_out, Opcode[3], not_44_out, Opcode[5]);
  and and_13 (FeDcBA_t, Opcode[0], Opcode[1], not_45_out, Opcode[3], not_46_out, Opcode[5]);
  and and_14 (FeDCba, not_47_out, not_48_out, Opcode[2], Opcode[3], not_49_out, Opcode[5]);
  and and_15 (and_15_out, not_68_out, not_69_out, not_70_out, not_71_out, not_72_out, Opcode[5]);
  and and_16 (and_16_out, not_73_out, not_74_out, not_75_out, Opcode[3], not_76_out, Opcode[5]);
  and and_17 (FeDcbA_t_t, Opcode[0], not_77_out, not_78_out, Opcode[3], not_79_out, Opcode[5]);
  or or_2 (Branch, fXdCba, fedCbA_t_t_t_t_t_t_t);
  or or_3 (or_3_out, Opcode[0], Opcode[1], Opcode[2], Opcode[3], Opcode[4], Opcode[5]);
  or or_4 (or_4_out, Opcode[0], Opcode[1], not_50_out, Opcode[3], Opcode[4], Opcode[5]);
  or or_5 (or_5_out, Opcode[0], Opcode[1], not_51_out, Opcode[3], not_52_out, Opcode[5]);
  or or_6 (or_6_out, not_53_out, Opcode[1], not_54_out, Opcode[3], Opcode[4], Opcode[5]);
  or or_7 (or_7_out, Opcode[0], Opcode[1], not_55_out, Opcode[3], Opcode[4], Opcode[5]);
  or or_8 (or_8_out, not_56_out, Opcode[1], not_57_out, Opcode[3], Opcode[4], Opcode[5]);
  or or_9 (or_9_out, Opcode[0], not_58_out, Opcode[2], Opcode[3], Opcode[4], Opcode[5]);
  or or_10 (or_10_out, Opcode[0], Opcode[1], Opcode[2], not_59_out, Opcode[4], not_60_out);
  or or_11 (or_11_out, not_61_out, Opcode[1], Opcode[2], not_62_out, Opcode[4], not_63_out);
  or or_12 (or_12_out, not_64_out, not_65_out, Opcode[2], not_66_out, Opcode[4], not_67_out);
  or or_13 (RegDst[0], fedcba_t_t_t_t_t_t_t_t_t, FeDCba);
  or or_14 (RegDst[1], fEdCba_t_t_t_t_t, fedcBA_t_t_t_t_t_t_t_t, FeDCba);
  or or_15 (ALUOp[0], fXdCba, fedCbA_t_t_t_t_t_t_t);
  or or_16 (ALUOp[1], fedcba_t_t_t_t_t_t_t_t_t, fedCbA_t_t_t_t_t_t_t);
  or or_17 (MemWrite, and_12_out, FeDcBA_t, FeDCba);
  and and_18 (ALUSrc, or_3_out, or_4_out, or_5_out, or_6_out);
  and and_19 (RegWrite, or_7_out, or_8_out, or_9_out, or_10_out, or_11_out, or_12_out);
  or or_18 (Unit[0], and_15_out, and_16_out, FeDcbA_t_t);
  or or_19 (Unit[1], FedCbA_t_t_t, FeDcbA_t_t);
  or or_20 (Unit[2], FedcBA_t_t_t_t, FeDcBA_t, FeDCba);
  or or_21 (MemtoReg[0], and_8_out, FedCbA_t_t_t, feDCBA_t_t_t_t_t_t, FedcBA_t_t_t_t);

  // Other names for the same wires on the sheet: Op0 = Opcode[0]; Op1 = Opcode[1]; Op2 = Opcode[2]; Op3 = Opcode[3];
  //   Op4 = Opcode[4]; Op5 = Opcode[5]
endmodule
