// Logisim project alu.circ as structural Verilog: 1 circuit, main circuit main
module main (
  input  [31:0] X,
  input  [31:0] Y,
  input  [3:0] Switch,
  output Signed_Overflow,
  output Equal,
  output [31:0] Result,
  output [31:0] Result_2
);

  wire and_2_out, and_3_out, and_4_out, and_5_out, and_6_out, bit_31_Out_minus, bit_31_Out_plus, carry_out,
       comparator_1_lt, comparator_2_lt, comparator_3_eq, comparator_4_eq, comparator_5_eq, comparator_6_eq,
       comparator_7_eq, comparator_8_eq, comparator_9_eq, comparator_10_eq, comparator_11_eq,
       comparator_12_eq, comparator_13_eq, comparator_14_eq, comparator_15_eq, comparator_16_eq,
       comparator_17_eq, neg, or_2_out, or_3_out, or_4_out, or_5_out, or_6_out;
  wire [4:0] bit_extender_1_out;
  wire [30:0] adder_1_out, subtractor_1_out;
  wire [31:0] adder_2_out, and_1_out, bit_extender_2_out, bit_extender_3_out, divider_1_out, divider_1_rem,
       multiplier_1_cout, multiplier_1_out, or_1_out, shifter_1_out, shifter_2_out, shifter_3_out,
       subtractor_2_out;

  Bit_Extender #(.in_width(32), .out_width(5)) bit_extender_1 (.in(Y), .out(bit_extender_1_out));
  Shifter #(.width(32)) shifter_1 (.in(X), .\dist (bit_extender_1_out), .out(shifter_1_out));
  Shifter #(.width(32), .shift("lr")) shifter_2 (.in(X), .\dist (bit_extender_1_out), .out(shifter_2_out));
  Shifter #(.width(32), .shift("ar")) shifter_3 (.in(X), .\dist (bit_extender_1_out), .out(shifter_3_out));
  Multiplier #(.width(32)) multiplier_1 (.a(X), .b(Y), .out(multiplier_1_out), .cout(multiplier_1_cout));  // open: cin
  Divider #(.width(32)) divider_1 (.a(X), .b(Y), .out(divider_1_out), .rem(divider_1_rem));  // open: upper
  Adder #(.width(32)) adder_1 (.a(X), .b(Y), .out({bit_31_Out_plus, adder_1_out}), .cout(carry_out));  // open: cin
  Adder #(.width(32)) adder_2 (.a(X), .b(Y), .out(adder_2_out));  // open: cin, cout
  Subtractor #(.width(32)) subtractor_1 (
    .a(X), .b(Y), .out({bit_31_Out_minus, subtractor_1_out}), .bout(neg));  // open: bin
  Subtractor #(.width(32)) subtractor_2 (.a(X), .b(Y), .out(subtractor_2_out));  // open: bin, bout
  assign and_1_out = X & Y;  // AND_Gate and_1, 32 bits wide
  assign or_1_out = X | Y;  // OR_Gate or_1, 32 bits wide
  Comparator #(.width(32)) comparator_1 (.a(X), .b(Y), .eq(Equal), .lt(comparator_1_lt));  // open: gt
  Comparator #(.width(32), .mode("unsigned")) comparator_2 (
    .a(X), .b(Y), .eq(Equal), .lt(comparator_2_lt));  // open: gt
  assign bit_extender_2_out = {{31{1'b0}}, comparator_1_lt};  // Bit_Extender bit_extender_2
  assign bit_extender_3_out = {{31{1'b0}}, comparator_2_lt};  // Bit_Extender bit_extender_3
  Multiplexer #(.select(4), .width(32)) multiplexer_1 (
    .in0(shifter_1_out), .in1(shifter_2_out), .in2(shifter_3_out), .in3(multiplier_1_out),
    .in4(divider_1_out), .in5({bit_31_Out_plus, adder_1_out}), .in6(adder_2_out),
    .in7({bit_31_Out_minus, subtractor_1_out}), .in8(subtractor_2_out), .in9(and_1_out), .in10(or_1_out),
    .in11(bit_extender_2_out), .in12(bit_extender_3_out), .in13({32{1'b0}}), .in14({32{1'b0}}),
    .in15({32{1'b0}}), .out(Result), .sel(Switch));  // open: en
  Multiplexer #(.select(4), .width(32)) multiplexer_2 (
    .in0({32{1'b0}}), .in1({32{1'b0}}), .in2({32{1'b0}}), .in3(multiplier_1_cout), .in4(divider_1_rem),
    .in5({32{1'b0}}), .in6({32{1'b0}}), .in7({32{1'b0}}), .in8({32{1'b0}}), .in9({32{1'b0}}),
    .in10({32{1'b0}}), .in11({32{1'b0}}), .in12({32{1'b0}}), .in13({32{1'b0}}), .in14({32{1'b0}}),
    .in15({32{1'b0}}), .out(Result_2), .sel(Switch));  // open: en
  Comparator #(.width(1), .mode("unsigned")) comparator_3 (.a(X[31]), .b(1'b0), .eq(comparator_3_eq));  // open: gt, lt
  Comparator #(.width(1), .mode("unsigned")) comparator_4 (.a(Y[31]), .b(1'b0), .eq(comparator_4_eq));  // open: gt, lt
  Comparator #(.width(1), .mode("unsigned")) comparator_5 (
    .a(bit_31_Out_plus), .b(1'b1), .eq(comparator_5_eq));  // open: gt, lt
  Comparator #(.width(1), .mode("unsigned")) comparator_6 (.a(X[31]), .b(1'b1), .eq(comparator_6_eq));  // open: gt, lt
  Comparator #(.width(1), .mode("unsigned")) comparator_7 (.a(Y[31]), .b(1'b1), .eq(comparator_7_eq));  // open: gt, lt
  Comparator #(.width(1), .mode("unsigned")) comparator_8 (
    .a(carry_out), .b(1'b1), .eq(comparator_8_eq));  // open: gt, lt
  Comparator #(.width(1), .mode("unsigned")) comparator_9 (.a(X[31]), .b(1'b1), .eq(comparator_9_eq));  // open: gt, lt
  Comparator #(.width(1), .mode("unsigned")) comparator_10 (
    .a(Y[31]), .b(1'b0), .eq(comparator_10_eq));  // open: gt, lt
  Comparator #(.width(1), .mode("unsigned")) comparator_11 (
    .a(bit_31_Out_minus), .b(1'b0), .eq(comparator_11_eq));  // open: gt, lt
  Comparator #(.width(1), .mode("unsigned")) comparator_12 (
    .a(X[31]), .b(1'b0), .eq(comparator_12_eq));  // open: gt, lt
  Comparator #(.width(1), .mode("unsigned")) comparator_13 (
    .a(Y[31]), .b(1'b1), .eq(comparator_13_eq));  // open: gt, lt
  Comparator #(.width(1), .mode("unsigned")) comparator_14 (
    .a(bit_31_Out_minus), .b(1'b1), .eq(comparator_14_eq));  // open: gt, lt
  Comparator #(.width(1), .mode("unsigned")) comparator_15 (
    .a(X[31]), .b(1'b1), .eq(comparator_15_eq));  // open: gt, lt
  Comparator #(.width(1), .mode("unsigned")) comparator_16 (
    .a(Y[31]), .b(1'b1), .eq(comparator_16_eq));  // open: gt, lt
  Comparator #(.width(1), .mode("unsigned")) comparator_17 (.a(neg), .b(1'b1), .eq(comparator_17_eq));  // open: gt, lt
  and and_2 (and_2_out, comparator_3_eq, comparator_4_eq, comparator_5_eq);
  or or_2 (or_2_out, comparator_6_eq, comparator_7_eq);
  and and_3 (and_3_out, comparator_9_eq, comparator_10_eq, comparator_11_eq);
  or or_3 (or_3_out, comparator_12_eq, comparator_13_eq);
  or or_4 (or_4_out, comparator_15_eq, comparator_16_eq);
  and and_4 (and_4_out, or_2_out, comparator_8_eq);
  and and_5 (and_5_out, or_3_out, comparator_14_eq);
  and and_6 (and_6_out, or_4_out, comparator_17_eq);
  or or_5 (or_5_out, and_2_out, and_4_out);
  or or_6 (or_6_out, and_3_out, and_5_out, and_6_out);
  Multiplexer #(.select(4)) multiplexer_3 (
    .in0(1'b0), .in1(1'b0), .in2(1'b0), .in3(1'b0), .in4(1'b0), .in5(or_5_out), .in6(1'b0), .in7(or_6_out),
    .in8(1'b0), .in9(1'b0), .in10(1'b0), .in11(1'b0), .in12(1'b0), .out(Signed_Overflow), .sel(Switch));  // open: in13, in14, in15, en

  // Other names for the same wires on the sheet: overflow = Signed_Overflow; S[3:0] = Switch; bit_31_X = X[31];
  //   bit_31_Y = Y[31]

  // Notes on the sheet:
  //   INPUTS to your circuit
  //   DON'T CHANGE THE LOCATIONS OF THE INPUTS AND OUTPUTS!
  //   OUTPUTS from your circuit
endmodule
