// Logisim project Ex1.circ as structural Verilog: 1 circuit, main circuit main
module main (
  output [15:0] F_n_2,
  output [15:0] out_2,
  output [15:0] f_n_1
);

  wire clk, clock_1_out, comparator_1_lt;
  wire [7:0] counter_1_q;

  Counter counter_1 (.count(comparator_1_lt), .Q(counter_1_q), .clk(clock_1_out));  // open: load, D, carry, clr
  Clock clock_1 (.out(clock_1_out));
  Comparator #(.mode("unsigned")) comparator_1 (.a(counter_1_q), .b(8'hf), .lt(comparator_1_lt));  // open: gt, eq
  Clock clock_2 (.out(clk));
  Register #(.width(16)) register_1 (.D(f_n_1), .en(comparator_1_lt), .Q(out_2), .clk(clk));  // open: clr
  // Probe on out_2
  Adder #(.width(16)) adder_1 (.a(out_2), .b(f_n_1), .out(F_n_2));  // open: cin, cout
  // Probe on F_n_2
  Register #(.width(16)) register_2 (.D(F_n_2), .en(comparator_1_lt), .Q(f_n_1), .clk(clk));  // open: clr
  // Probe on f_n_1

  // Notes on the sheet:
  //   f(n)
endmodule
